# Fritzing sketch Esboço_Projeto (saved by Fritzing 0.9.3b)
breadboards: 1

parts:
  HC-SR04_Sensor_1 = HC-SR04 Ultrasonic Distance Sensor
  R2 = Resistor [tolerance=±5% resistance=1k package=THT]  # not connected
  R1 = Resistor [tolerance=±5% resistance=1k package="2512 [SMD]"]
  R3 = Resistor [tolerance=±5% resistance=1k package=THT]
  R4 = Resistor [tolerance=±5% resistance=1k package=THT]
  U2 = ESP32-38PinWide [part_number=ESP32-38PinWide]
  R5 = Resistor [tolerance=±5% resistance=1k package=THT]
  R6 = Resistor [tolerance=±5% resistance=1k package=THT]

nets:
  VCC: HC-SR04_Sensor_1.VCC, R3.Pin_1, R4.Pin_1, U2.GPIO34, U2.GPIO35, U2.GPIO32, U2.GPIO33, U2.VIN, R5.Pin_1, R6.Pin_1
  N1: HC-SR04_Sensor_1.TRIG, U2.GPIO27
  N2: HC-SR04_Sensor_1.GND, R1.Pin_0, R3.Pin_0, R4.Pin_0, U2.GPIO11, R5.Pin_0, R6.Pin_0
  N3: R1.Pin_1, U2.GPIO14

notes:
  Sensor2
  Sensor1
  Sensor3
  Sensor4

custom parts:
  ESP32-38PinWide: Generic 38-Pin ESP32 with wide format (only access to one side of pins on a breadboard) based on Stephen Lilley's HiLetgo ESP-WROOM-32 ESP32 ESP-32S Development Board.
